// Logisim project SixteenBitProzessor.circ as structural Verilog: 8 circuits, main circuit GatedMove
module EQU (
  input  I0,
  input  I1,
  output O0
);

  wire and_1_out, nor_1_out;

  and and_1 (and_1_out, I1, I0);
  nor nor_1 (nor_1_out, I0, I1);
  or or_1 (O0, and_1_out, nor_1_out);
endmodule

module GatedMove (
  input  Enable,
  input  I0,
  output Valid,
  output Q0
);

  wire not_1_out, or_1_out;

  not not_1 (not_1_out, Enable);
  and and_1 (Q0, Enable, I0);
  EQU Gleich (.I0(Q0), .I1(or_1_out), .O0(Valid));
  or or_1 (or_1_out, I0, not_1_out);
endmodule

module TestGatedMove (
  input  En_in,
  input  I0,
  output En_out,
  output O0
);

  GatedMove TestGatedMove (.Enable(En_in), .I0(I0), .Valid(En_out), .Q0(O0));
endmodule

module DualRailNAND (
  input  A,
  input  B,
  input  A_En,
  input  B_En,
  output Out0,
  output OutValid
);

  wire and_1_out, nand_1_out;

  nand nand_1 (nand_1_out, A, B);
  and and_1 (and_1_out, A_En, B_En);
  GatedMove gatedmove_1 (.Enable(nand_1_out), .I0(and_1_out), .Valid(Out0), .Q0(OutValid));
endmodule

module EightGatedMove (
  input  EnIn,
  input  [7:0] In0To8,
  output EnOut,
  output [7:0] Out0To8
);

  wire gatedmove_1_valid, gatedmove_2_valid, gatedmove_3_valid, gatedmove_4_valid, gatedmove_5_valid,
       gatedmove_6_valid, gatedmove_7_valid, gatedmove_8_valid;

  GatedMove gatedmove_1 (.Enable(EnIn), .I0(In0To8[0]), .Valid(gatedmove_1_valid), .Q0(Out0To8[0]));
  GatedMove gatedmove_2 (.Enable(EnIn), .I0(In0To8[1]), .Valid(gatedmove_2_valid), .Q0(Out0To8[1]));
  GatedMove gatedmove_3 (.Enable(EnIn), .I0(In0To8[2]), .Valid(gatedmove_3_valid), .Q0(Out0To8[2]));
  GatedMove gatedmove_4 (.Enable(EnIn), .I0(In0To8[3]), .Valid(gatedmove_4_valid), .Q0(Out0To8[3]));
  GatedMove gatedmove_5 (.Enable(EnIn), .I0(In0To8[4]), .Valid(gatedmove_5_valid), .Q0(Out0To8[4]));
  GatedMove gatedmove_6 (.Enable(EnIn), .I0(In0To8[5]), .Valid(gatedmove_6_valid), .Q0(Out0To8[5]));
  GatedMove gatedmove_7 (.Enable(EnIn), .I0(In0To8[6]), .Valid(gatedmove_7_valid), .Q0(Out0To8[6]));
  GatedMove gatedmove_8 (.Enable(EnIn), .I0(In0To8[7]), .Valid(gatedmove_8_valid), .Q0(Out0To8[7]));
  and AOut (EnOut, gatedmove_1_valid, gatedmove_2_valid, gatedmove_3_valid, gatedmove_4_valid, gatedmove_5_valid, gatedmove_6_valid, gatedmove_7_valid, gatedmove_8_valid);
endmodule

module SixteenGatedMove (
  input  EnIn,
  input  [15:0] In0To16,
  output EnOut,
  output [15:0] Out0To16
);

  wire eightgatedmove_1_enout, eightgatedmove_2_enout;

  EightGatedMove eightgatedmove_1 (
    .EnIn(EnIn), .In0To8(In0To16[7:0]), .EnOut(eightgatedmove_1_enout), .Out0To8(Out0To16[7:0]));
  EightGatedMove eightgatedmove_2 (
    .EnIn(EnIn), .In0To8(In0To16[15:8]), .EnOut(eightgatedmove_2_enout), .Out0To8(Out0To16[15:8]));
  and AndEn (EnOut, eightgatedmove_1_enout, eightgatedmove_2_enout);
endmodule

module CPU16_Regs (
  input  ExecEn,
  input  CommitEn,
  input  NPC_in00,
  input  NPC_in01,
  input  NPC_in02,
  input  NPC_in03,
  input  NPC_in04,
  input  NPC_in05,
  input  NPC_in06,
  input  NPC_in07,
  input  NPC_in08,
  input  NPC_in09,
  input  NPC_in10,
  input  NPC_in11,
  input  NPC_in12,
  input  NPC_in13,
  input  NPC_in14,
  input  NPC_in15,
  input  A_in00,
  input  A_in01,
  input  A_in02,
  input  A_in03,
  input  A_in04,
  input  A_in05,
  input  A_in06,
  input  A_in07,
  input  ADDR_in00,
  input  ADDR_in01,
  input  ADDR_in02,
  input  ADDR_in03,
  input  ADDR_in04,
  input  ADDR_in05,
  input  ADDR_in06,
  input  ADDR_in07,
  input  ADDR_in08,
  input  ADDR_in09,
  input  ADDR_in10,
  input  ADDR_in11,
  input  ADDR_in12,
  input  ADDR_in13,
  input  ADDR_in14,
  input  ADDR_in15,
  output ExecEnOut,
  output CommitEnOut,
  output NPC_out00,
  output PC_out00,
  output NPC_out01,
  output PC_out01,
  output NPC_out02,
  output PC_out02,
  output NPC_out03,
  output PC_out03,
  output NPC_out04,
  output PC_out04,
  output NPC_out05,
  output PC_out05,
  output NPC_out06,
  output PC_out06,
  output NPC_out07,
  output PC_out07,
  output NPC_out08,
  output PC_out08,
  output NPC_out09,
  output PC_out09,
  output NPC_out10,
  output PC_out10,
  output NPC_out11,
  output PC_out11,
  output NPC_out12,
  output PC_out12,
  output NPC_out13,
  output PC_out13,
  output NPC_out14,
  output PC_out14,
  output NPC_out15,
  output PC_out15,
  output A_out00,
  output A_out01,
  output A_out02,
  output A_out03,
  output A_out04,
  output A_out05,
  output A_out06,
  output A_out07,
  output ADDR_out00,
  output ADDR_out01,
  output ADDR_out02,
  output ADDR_out03,
  output ADDR_out04,
  output ADDR_out05,
  output ADDR_out06,
  output ADDR_out07,
  output ADDR_out08,
  output ADDR_out09,
  output ADDR_out10,
  output ADDR_out11,
  output ADDR_out12,
  output ADDR_out13,
  output ADDR_out14,
  output ADDR_out15
);

  wire eightgatedmove_1_enout, sixteengatedmove_1_enout, sixteengatedmove_2_enout;

  SixteenGatedMove sixteengatedmove_1 (
    .EnIn(ExecEn),
    .In0To16({NPC_in15, NPC_in14, NPC_in13, NPC_in12, NPC_in11, NPC_in10, NPC_in09, NPC_in08, NPC_in07, NPC_in06, NPC_in05, NPC_in04, NPC_in03, NPC_in02, NPC_in01, NPC_in00}),
    .EnOut(sixteengatedmove_1_enout),
    .Out0To16({PC_out15, PC_out14, PC_out13, PC_out12, PC_out11, PC_out10, PC_out09, PC_out08, PC_out07, PC_out06, PC_out05, PC_out04, PC_out03, PC_out02, PC_out01, PC_out00}));
  EightGatedMove eightgatedmove_1 (
    .EnIn(ExecEn), .In0To8({A_in07, A_in06, A_in05, A_in04, A_in03, A_in02, A_in01, A_in00}),
    .EnOut(eightgatedmove_1_enout),
    .Out0To8({A_out07, A_out06, A_out05, A_out04, A_out03, A_out02, A_out01, A_out00}));
  SixteenGatedMove sixteengatedmove_2 (
    .EnIn(ExecEn),
    .In0To16({ADDR_in15, ADDR_in14, ADDR_in13, ADDR_in12, ADDR_in11, ADDR_in10, ADDR_in09, ADDR_in08, ADDR_in07, ADDR_in06, ADDR_in05, ADDR_in04, ADDR_in03, ADDR_in02, ADDR_in01, ADDR_in00}),
    .EnOut(sixteengatedmove_2_enout),
    .Out0To16({ADDR_out15, ADDR_out14, ADDR_out13, ADDR_out12, ADDR_out11, ADDR_out10, ADDR_out09, ADDR_out08, ADDR_out07, ADDR_out06, ADDR_out05, ADDR_out04, ADDR_out03, ADDR_out02, ADDR_out01, ADDR_out00}));
  SixteenGatedMove sixteengatedmove_3 (
    .EnIn(CommitEn),
    .In0To16({PC_out15, PC_out14, PC_out13, PC_out12, PC_out11, PC_out10, PC_out09, PC_out08, PC_out07, PC_out06, PC_out05, PC_out04, PC_out03, PC_out02, PC_out01, PC_out00}),
    .EnOut(CommitEnOut),
    .Out0To16({NPC_out15, NPC_out14, NPC_out13, NPC_out12, NPC_out11, NPC_out10, NPC_out09, NPC_out08, NPC_out07, NPC_out06, NPC_out05, NPC_out04, NPC_out03, NPC_out02, NPC_out01, NPC_out00}));
  and AndOut (ExecEnOut, sixteengatedmove_1_enout, eightgatedmove_1_enout, sixteengatedmove_2_enout);
endmodule

module PCPlus1Adder16 (
  input  PC_in00,
  input  PC_in01,
  input  PC_in02,
  input  PC_in03,
  input  PC_in04,
  input  PC_in05,
  input  PC_in06,
  input  PC_in07,
  input  PC_in08,
  input  PC_in09,
  input  PC_in10,
  input  PC_in11,
  input  PC_in12,
  input  PC_in13,
  input  PC_in14,
  input  PC_in15,
  output PC_out00,
  output PC_out01,
  output PC_out02,
  output PC_out03,
  output PC_out04,
  output PC_out05,
  output PC_out06,
  output PC_out07,
  output PC_out08,
  output PC_out09,
  output PC_out10,
  output PC_out11,
  output PC_out12,
  output PC_out13,
  output PC_out14,
  output PC_out15
);

  Adder #(.width(16)) adder_1 (
    .a({PC_in15, PC_in14, PC_in13, PC_in12, PC_in11, PC_in10, PC_in09, PC_in08, PC_in07, PC_in06, PC_in05, PC_in04, PC_in03, PC_in02, PC_in01, PC_in00}),
    .b(16'h1),
    .out({PC_out15, PC_out14, PC_out13, PC_out12, PC_out11, PC_out10, PC_out09, PC_out08, PC_out07, PC_out06, PC_out05, PC_out04, PC_out03, PC_out02, PC_out01, PC_out00}));  // open: cin, cout
endmodule
